// Logisim project circuit_diagram.circ as structural Verilog: 17 circuits, main circuit main
module main (
);

  wire battery_1_battery_negative, battery_1_battery_positive, connector_1_connector_out_negative,
       connector_1_connector_out_positive, connector_2_connector_out_negative,
       connector_2_connector_out_positive, connector_4_connector_out_negative,
       connector_4_connector_out_positive, fsky_fsesc_mini_v6dot7_pro_1_motor_a,
       fsky_fsesc_mini_v6dot7_pro_1_motor_b, fsky_fsesc_mini_v6dot7_pro_1_motor_c,
       fsky_fsesc_mini_v6dot7_pro_1_receiver_5v, fsky_fsesc_mini_v6dot7_pro_1_receiver_negative,
       fsky_fsesc_mini_v6dot7_pro_1_receiver_signal, jetson_1_dc_negative, jetson_1_dc_positive,
       regulator_current_protection_1_output_negative, regulator_current_protection_1_output_positive,
       Screen, undriven, voltage_converter_1_out1_negative, voltage_converter_1_out1_positive,
       voltage_converter_1_out2_negative, voltage_converter_1_out2_positive;
  wire [3:0] jetson_1_usb1, jetson_1_usb2, jetson_1_usb3, jetson_1_usb4, Keyboard,
       ld_control_speed_board_v1_1_pin1, Mouse, usb_hub_1_port_out1, usb_hub_1_port_out2, wall_power_supply;
  wire [5:0] drive_motor_1_sensor;

  Battery battery_1 (.Battery_positive(battery_1_battery_positive), .Battery_negative(battery_1_battery_negative));
  connector connector_1 (
    .connector_out_positive(connector_1_connector_out_positive),
    .connector_out_negative(connector_1_connector_out_negative),
    .connector_in_positive(battery_1_battery_positive), .connector_in_negative(battery_1_battery_negative));
  Voltage_converter voltage_converter_1 (
    .out2_positive(voltage_converter_1_out2_positive), .out2_negative(voltage_converter_1_out2_negative),
    .out1_positive(voltage_converter_1_out1_positive), .out1_negative(voltage_converter_1_out1_negative),
    .Battery_in_negative(connector_4_connector_out_negative),
    .Battery_in_positive(connector_4_connector_out_positive));
  regulator_current_protection regulator_current_protection_1 (
    .output_negative(regulator_current_protection_1_output_negative),
    .output_positive(regulator_current_protection_1_output_positive),
    .battery_negative(connector_1_connector_out_negative),
    .battery_positive(connector_1_connector_out_positive));  // open: pin1, pin2, pin3
  connector connector_2 (
    .connector_out_positive(connector_2_connector_out_positive),
    .connector_out_negative(connector_2_connector_out_negative),
    .connector_in_positive(regulator_current_protection_1_output_positive),
    .connector_in_negative(regulator_current_protection_1_output_negative));
  jetson jetson_1 (
    .USB1(jetson_1_usb1), .USB2(jetson_1_usb2), .USB3(jetson_1_usb3), .USB4(jetson_1_usb4), .hdmi_in(Screen),
    .DC_positive(jetson_1_dc_positive), .DC_negative(jetson_1_dc_negative),
    .micro_usb_positive(wall_power_supply[3]), .micro_usb_data_negative(wall_power_supply[2]),
    .micro_usb_data_positive(wall_power_supply[1]), .micro_usb_negative(wall_power_supply[0]),
    .jumper_pin1(undriven), .jumper_pin2(undriven));  // open: Display_port_in, ETHERNET
  connector connector_3 (
    .connector_in_positive(voltage_converter_1_out2_positive),
    .connector_in_negative(voltage_converter_1_out2_negative));  // open: connector_out_positive, connector_out_negative
  barrel_jack barrel_jack_1 (
    .positive(jetson_1_dc_negative), .negative(jetson_1_dc_positive),
    .wire_positive(voltage_converter_1_out1_positive), .wire_negative(voltage_converter_1_out1_negative));
  connector connector_4 (
    .connector_out_positive(connector_4_connector_out_positive),
    .connector_out_negative(connector_4_connector_out_negative),
    .connector_in_positive(connector_2_connector_out_positive),
    .connector_in_negative(connector_2_connector_out_negative));
  drive_motor drive_motor_1 (
    .Sensor(drive_motor_1_sensor), .B(fsky_fsesc_mini_v6dot7_pro_1_motor_b),
    .C(fsky_fsesc_mini_v6dot7_pro_1_motor_c), .A(fsky_fsesc_mini_v6dot7_pro_1_motor_a));
  LD_CONTROL_SPEED_BOARD_V1 ld_control_speed_board_v1_1 (
    .pin1(ld_control_speed_board_v1_1_pin1[0]), .pin2(ld_control_speed_board_v1_1_pin1[1]),
    .pin3(ld_control_speed_board_v1_1_pin1[2]), .pin4(ld_control_speed_board_v1_1_pin1[3]),
    .usb_5v_negative(jetson_1_usb2[0]), .usb_data_plus(jetson_1_usb2[1]), .usb_data_minus(jetson_1_usb2[2]),
    .usb_5v_positive(jetson_1_usb2[3]));
  Fsky_Fsesc_Mini_V6dot7_Pro fsky_fsesc_mini_v6dot7_pro_1 (
    .motor_A(fsky_fsesc_mini_v6dot7_pro_1_motor_a), .motor_B(fsky_fsesc_mini_v6dot7_pro_1_motor_b),
    .motor_C(fsky_fsesc_mini_v6dot7_pro_1_motor_c), .sense_5v(drive_motor_1_sensor[5]),
    .sense_tmp(drive_motor_1_sensor[4]), .sense_H1(drive_motor_1_sensor[3]),
    .sense_H2(drive_motor_1_sensor[2]), .sense_H3(drive_motor_1_sensor[1]),
    .sense_NEGATIVE(drive_motor_1_sensor[0]), .usb_5v_negative(jetson_1_usb3[0]),
    .usb_data_plus(jetson_1_usb3[1]), .receiver_negative(fsky_fsesc_mini_v6dot7_pro_1_receiver_negative),
    .usb_data_minus(jetson_1_usb3[2]), .receiver_5v(fsky_fsesc_mini_v6dot7_pro_1_receiver_5v),
    .usb_5v_positive(jetson_1_usb3[3]), .receiver_signal(fsky_fsesc_mini_v6dot7_pro_1_receiver_signal),
    .battery_negative(connector_2_connector_out_negative),
    .battery_positive(connector_2_connector_out_positive));  // open: comm_5v, comm_3dot3v, comm_negative, comm_ADC1, comm_RX_or_SDA, comm_TX_or_SCL, comm_ADC2, comm_ADC3, swd_3dot3v, swd_swclk, can_5v, swd_negative, can_CAH, swd_swdio, can_CAL, swd_nrst, can_NEGATIVE
  usb_hub usb_hub_1 (
    .port_out1(usb_hub_1_port_out1), .port_out2(usb_hub_1_port_out2), .port_out3(Mouse),
    .port_out4(Keyboard), .port_in(jetson_1_usb1));
  cervo_motor cervo_motor_1 (
    .cervo_positive(fsky_fsesc_mini_v6dot7_pro_1_receiver_negative),
    .cervo_negative(fsky_fsesc_mini_v6dot7_pro_1_receiver_5v),
    .cervo_signal(fsky_fsesc_mini_v6dot7_pro_1_receiver_signal));
  Lidar lidar_1 (
    .lidar_input_1(ld_control_speed_board_v1_1_pin1[0]), .lidar_input_2(ld_control_speed_board_v1_1_pin1[1]),
    .lidar_input_3(ld_control_speed_board_v1_1_pin1[2]), .lidar_input_4(ld_control_speed_board_v1_1_pin1[3]));
  wifi_dongle wifi_dongle_1 (.usb_male(jetson_1_usb4));
  remote_controler remote_controler_1 (.bluetooth_dongle(usb_hub_1_port_out1));
  Camera camera_1 (.type_c_in(usb_hub_1_port_out2));
endmodule

module Fsky_Fsesc_Mini_V6dot7_Pro (
  input  battery_negative,
  input  battery_positive,
  output comm_5v,
  output comm_3dot3v,
  output comm_negative,
  output comm_ADC1,
  output comm_RX_or_SDA,
  output comm_TX_or_SCL,
  output comm_ADC2,
  output comm_ADC3,
  output swd_3dot3v,
  output swd_swclk,
  output swd_negative,
  output swd_swdio,
  output swd_nrst,
  output motor_A,
  output motor_B,
  output motor_C,
  output receiver_negative,
  output receiver_5v,
  output receiver_signal,
  output sense_5v,
  output sense_tmp,
  output sense_H1,
  output sense_H2,
  output sense_H3,
  output sense_NEGATIVE,
  output usb_5v_negative,
  output usb_data_plus,
  output usb_data_minus,
  output usb_5v_positive,
  output can_5v,
  output can_CAH,
  output can_CAL,
  output can_NEGATIVE
);
endmodule

module Battery (
  output Battery_positive,
  output Battery_negative
);


  // Notes on the sheet:
  //   Battery_positive: pull=up
endmodule

module jetson (
  input  jumper_pin1,
  input  jumper_pin2,
  input  ETHERNET,
  output [3:0] USB1,
  output [3:0] USB2,
  output [3:0] USB3,
  output [3:0] USB4,
  output hdmi_in,
  output Display_port_in,
  output micro_usb_positive,
  output DC_positive,
  output micro_usb_data_negative,
  output DC_negative,
  output micro_usb_data_positive,
  output micro_usb_negative
);
endmodule

module cervo_motor (
  input  cervo_positive,
  input  cervo_negative,
  input  cervo_signal
);
endmodule

module drive_motor (
  input  A,
  input  B,
  input  C,
  output [5:0] Sensor
);
endmodule

module Voltage_converter (
  input  Battery_in_positive,
  input  Battery_in_negative,
  output out1_positive,
  output out1_negative,
  output out2_positive,
  output out2_negative
);
endmodule

module regulator (
  input  in_1,
  input  in_2
);
endmodule

module regulator_current_protection (
  input  battery_positive,
  input  battery_negative,
  output output_positive,
  output output_negative,
  output pin1,
  output pin2,
  output pin3
);
endmodule

module connector (
  input  connector_in_positive,
  input  connector_in_negative,
  output connector_out_positive,
  output connector_out_negative
);
endmodule

module barrel_jack (
  input  wire_positive,
  input  wire_negative,
  output positive,
  output negative
);
endmodule

module LD_CONTROL_SPEED_BOARD_V1 (
  input  usb_5v_negative,
  input  usb_data_plus,
  input  usb_data_minus,
  input  usb_5v_positive,
  output pin1,
  output pin2,
  output pin3,
  output pin4
);
endmodule

module Lidar (
  input  lidar_input_1,
  input  lidar_input_2,
  input  lidar_input_3,
  input  lidar_input_4
);
endmodule

module wifi_dongle (
  output [3:0] usb_male
);
endmodule

module usb_hub (
  input  [3:0] port_in,
  output [3:0] port_out4,
  output [3:0] port_out3,
  output [3:0] port_out2,
  output [3:0] port_out1
);


  assign port_out1 = port_in;
  assign port_out2 = port_in;
  assign port_out3 = port_in;
  assign port_out4 = port_in;
endmodule

module remote_controler (
  input  [3:0] bluetooth_dongle
);
endmodule

module Camera (
  input  [3:0] type_c_in
);
endmodule
